# Fritzing sketch HelloDisplay (saved by Fritzing 0.9.3b)
breadboards: 1

parts:
  Part1 = Arduino Mega ADK (Rev3)
  R1 = Resistor [tolerance=±5% resistance=220 package="0805 [SMD]"]
  J1 = Piezo Speaker

nets:
  N1: Part1.GND, J1.pin1
  N2: Part1.D8_PWM, R1.Pin_1
  N3: R1.Pin_0, J1.pin2
